# Fritzing sketch core-sketch (saved by Fritzing 0.9.3b)
breadboards: 1

parts:
  Part1 = Arduino Uno (Rev3)
  LED1 = LED - 5mm [color="Red (633nm)" package="5 mm [THT]"]
  LED2 = LED - 5mm [color="Green (565nm)" package="5 mm [THT]"]
  R1 = Photocell (LDR) [package=THT]
  J1 = Piezo Speaker  # not connected

nets:
  N1: Part1.A0, R1.pin_1
  N2: Part1.GND, LED1.cathode, LED2.cathode
  N3: Part1.D0/RX, LED1.anode
  N4: Part1.D3_PWM, LED2.anode
  N5: Part1.5V, R1.pin_0
